# Fritzing sketch MPU6050-Nokia5110-Leonardo (saved by Fritzing 0.8.7b)
circuit board: 8.46667cm x 5.64444cm
breadboards: 1

parts:
  Nokia_5110_LCD_Module1 = Nokia5110LCDModule
  GY1 = MPU-6050 Board GY-521 [form="♀ (female)" package=THT]
  Part1 = Arduino Leonardo (Rev3b)
  R1 = Resistor [tolerance=±5% resistance=220 package=THT]

nets:
  VCC: Nokia_5110_LCD_Module1.Vcc, GY1.pin1, Part1.5V, R1.Pin_0
  N1: Nokia_5110_LCD_Module1.Grnd, GY1.pin2, Part1.GND
  N2: Nokia_5110_LCD_Module1.SCE, Part1.D8/A8
  N3: Nokia_5110_LCD_Module1.RST, Part1.D7
  N4: Nokia_5110_LCD_Module1.D/C, Part1.D6_PWM/A7
  N5: Nokia_5110_LCD_Module1.6_DN_(MOSI), Part1.D5_PWM
  N6: Nokia_5110_LCD_Module1.SCLK, Part1.D4/A6
  N7: Nokia_5110_LCD_Module1.LED, R1.Pin_1
  N8: GY1.pin3, Part1.D3_PWM/SCL, Part1.SCL
  N9: GY1.pin4, Part1.D2/SDA, Part1.SDA

custom parts:
  : Nokia 5110 LCD with 8 pin. It's a 45mm*45mm module part. Description: The Nokia 5110 is a basic graphic LCD screen for lots of applications. It was originally intended for as a cell phone screen. This one is mounted on an easy to solder PCB. It uses the PCD8544 controller. The PCD8544 is a low power CMOS LCD controller/driver, designed to drive a graphic display of 48 rows and 84 columns. All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
  MPU-6050 Board GY-521: Acelerometro y Giroscopio MPU-6050 Board GY-521
